# Fritzing sketch AirMonitoring-Esp32-WiringDiagram (saved by Fritzing 1.0.6)
breadboards: 1

parts:
  M1 = FireBeetle ESP32-E
  Mod1 = Passive Buzzer
  Mod2 = MQ-7 breakout
  Part1 = BME280 Breakout

nets:
  N1: M1.pin_7, Mod2.AO
  N2: M1.pin_10, M1.pin_26, Part1.SDI/SDA
  N3: M1.pin_11, M1.pin_25, Part1.SCK/SCL
  GND: M1.pin_12, M1.pin_20, Mod1.-, Mod2.GND, Part1.GND
  N4: M1.pin_13, Mod1.NC, Part1.3.3V
  N5: M1.pin_14, Mod2.VCC
  N6: M1.pin_31, Mod1.S
  N7: M1.pin_32, Mod2.DO

custom parts:
  FireBeetle ESP32-E: FireBeetle ESP32-E, specially designed for IoT, is an ESP-WROOM-32E-based main controller board with dual-core chips. It supports WiFi and Bluetooth dual-mode communication and features a small size, ultra-low power consumption, on-board charging circuit, and easy-to-use interface, which can be conveniently used for smart home IoT, industrial IoT applications, wearable devices, and so on. You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
  MQ-7 breakout: MQ-5 gas sensor
